# Fritzing sketch accel_servo (saved by Fritzing 1.0.1rc)
breadboards: 1

parts:
  A1 = photon2
  J1 = Basic Servo
  Part2 = Adafruit ADXL345 [part_number="Adafruit #1231"]

nets:
  VCC: A1.Pin_2, J1.vcc, Part2.VIN
  GND: A1.Pin_4, A1.Pin_30, J1.gnd, Part2.GND
  N1: A1.Pin_10, Part2.CS
  N2: A1.Pin_11, Part2.SCL
  N3: A1.Pin_12, Part2.SDA/SDIO
  N4: A1.Pin_13, Part2.SDO/ADDR
  N5: A1.Pin_18, J1.pulse
  N6: A1.Pin_28, A1.Pin_29

notes:
  ADXL362

custom parts:
  photon2: The Photon 2 is a development module with a microcontroller and Wi-Fi networking.
  Adafruit ADXL345: Filling out our accelerometer offerings, we now have the really lovely digital ADXL345 from Analog Devices, a triple-axis accelerometer with digital I2C and SPI interface breakout. We added an on-board 3.3V regulator and logic-level shifting circuitry, making it a perfect choice for interfacing with any 3V or 5V microcontroller such as the Arduino. The sensor has three axes of measurements, X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
