# Fritzing sketch button_led_pulse (saved by Fritzing 1.0.1rc)
breadboards: 1

parts:
  R1 = Resistor [tolerance=±5% power=0.25W resistance=330 package=THT]  # not connected
  LED1 = LED - 5mm [color="Green (565nm)" current=0.030A package="5 mm [THT]"]
  A1 = photon2
  S6 = Pushbutton [package=THT]  # not connected

nets:
  N1: LED1.cathode, A1.Pin_4, A1.Pin_30, A1.Pin_32
  N2: A1.Pin_28, A1.Pin_29

custom parts:
  photon2: The Photon 2 is a development module with a microcontroller and Wi-Fi networking.
