# Fritzing sketch basic_button_soc (saved by Fritzing 1.0.1rc)
breadboards: 1

parts:
  A1 = photon2
  S2 = Pushbutton [package=THT]

nets:
  N1: A1.Pin_2, S2.leg0
  N2: A1.Pin_4, A1.Pin_30
  N3: A1.Pin_25, S2.leg1
  N4: A1.Pin_28, A1.Pin_29

custom parts:
  photon2: The Photon 2 is a development module with a microcontroller and Wi-Fi networking.
