# Fritzing sketch fsr_to_ledcolor (saved by Fritzing 1.0.1rc)
breadboards: 1

parts:
  LED1 = RGB LED (com. cathode, rgb) [color="Red (633nm)" current=0.030A package="5 mm [THT]"]
  R2 = Basic Force Sensing Resistor (FSR) [package=THT]
  A1 = photon2
  R3 = Resistor [tolerance=±5% power=0.25W resistance=220 package=THT]

nets:
  N1: LED1.red_anode, A1.Pin_7
  N2: LED1.common_cathode, A1.Pin_4, A1.Pin_30, R3.Pin_1
  N3: LED1.green_anode, A1.Pin_8
  N4: LED1.blue_anode, A1.Pin_12
  N5: R2.pin_1, A1.Pin_2, A1.Pin_31
  N6: R2.pin_2, A1.Pin_6, R3.Pin_0
  N7: A1.Pin_28, A1.Pin_29

custom parts:
  photon2: The Photon 2 is a development module with a microcontroller and Wi-Fi networking.
