# Fritzing sketch accelgyro (saved by Fritzing 1.0.1rc)
breadboards: 2

parts:
  A1 = photon2
  Part1 = InvenSense MPU6050
  A2 = photon2
  S3 = Pushbutton [package=THT]

nets:
  N1: A1.Pin_2, A1.Pin_31, Part1.VCC
  N2: A1.Pin_4, A1.Pin_30, A1.Pin_35, Part1.GND
  N3: A1.Pin_17, Part1.SDA
  N4: A1.Pin_18, Part1.SCL
  N5: A1.Pin_28, A1.Pin_29
  N6: A2.Pin_2, S3.leg0
  N7: A2.Pin_4, A2.Pin_30
  N8: A2.Pin_20, S3.leg1
  N9: A2.Pin_28, A2.Pin_29

notes:
  this particular wiring diagram might only be useful for wiring an MPU6050 via the pads on the PCB. Note that the stemma/qt interfacing board is not shown here as it's a difficult thing to represent in fritzing.
  this gives you an idea of how things are connected between the 4-pin connector at the photon board when you use the stemma/qt cable connection, but is not a representation of that.
  if you are connecting your photon2 to the MPU6050 with stemma you can ignore this diagram.
  This wiring diagram is for the button only. Use it to employ the button functionality found in the code. It is optional, but might be fun to play around with.
  You'll note that the number of rail spaces on the breadboard might differ from the exact button you have in the kit.

custom parts:
  photon2: The Photon 2 is a development module with a microcontroller and Wi-Fi networking.
