# Fritzing sketch apds9960 (saved by Fritzing 1.0.1rc)
breadboards: 1

parts:
  A1 = photon2
  Part1 = Adafruit APDS-9960 [part_number="Adafruit #3595"]

nets:
  N1: A1.Pin_2, A1.Pin_31, Part1.3.3V
  N2: A1.Pin_4, A1.Pin_30, A1.Pin_35, Part1.GND
  N3: A1.Pin_17, Part1.SDA
  N4: A1.Pin_18, Part1.SCL
  N5: A1.Pin_20, Part1.INT
  N6: A1.Pin_28, A1.Pin_29

notes:
  this particular wiring diagram might only be useful for wiring an APDS9960 via the pads on the PCB. Note that the stemma/qt interfacing board is not shown here as it's a difficult thing to represent in fritzing (and also that there is no reason to use the stemma interfacing board if you are going to wire directly).
  this gives you an idea of how things are connected between the 4-pin connector at the photon board when you use the stemma/qt cable connection, but is not a representation of that.
  if you are connecting your photon2 to the APDS9960 with stemma you can ignore this diagram.

custom parts:
  photon2: The Photon 2 is a development module with a microcontroller and Wi-Fi networking.
  Adafruit APDS-9960: The APDS9960 from Avago Technologies has an integrated IR LED and driver, along with four directional photodiodes that sense reflected IR energy from the LED. It's proximity detection feature allows it to measure the distance an object is from the front of the sensor (up to a few centimeters) with 8 bit resolution. Since there are four IR sensors, you can measure the changes in light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
