# Fritzing sketch haptic_motor (saved by Fritzing 1.0.1rc)
breadboards: 2

parts:
  A1 = photon2
  A2 = photon2
  S3 = Pushbutton [package=THT]
  Adafruit#1 = Adafruit DRV2605L Haptic Motor Controller - STEMMA QT [part_number=2305]
  MOTOR1 = Vibration Motor

nets:
  N1: A1.Pin_4, A1.Pin_30
  N2: A1.Pin_17, Adafruit#1.SDA
  N3: A1.Pin_18, Adafruit#1.SCL
  N4: A1.Pin_28, A1.Pin_29
  N5: A2.Pin_2, S3.leg0
  N6: A2.Pin_4, A2.Pin_30
  N7: A2.Pin_19, S3.leg1
  N8: A2.Pin_28, A2.Pin_29
  N9: Adafruit#1.OUT+, MOTOR1.POS
  N10: Adafruit#1.OUT-, MOTOR1.NEG

notes:
  this particular wiring diagram might only be useful for wiring an DRV2605L via the pads on the PCB. Note that the stemma/qt interfacing board is not shown here as it's a difficult thing to represent in fritzing.
  this gives you an idea of how things are connected between the 4-pin connector at the photon board when you use the stemma/qt cable connection, but is not a representation of that.
  if you are connecting your photon2 to the DRV2605L with stemma you can ignore this diagram.
  This wiring diagram is for the button only. Use it to employ the button functionality found in the code. It is optional, but might be fun to play around with.
  You'll note that the number of rail spaces on the breadboard might differ from the exact button you have in the kit.
  this is the way the vibration motor
  is connected to the DRV2605L. Note that there is strain relief recommended, which can be found in a tutorial video example linked inside of the README.md

custom parts:
  photon2: The Photon 2 is a development module with a microcontroller and Wi-Fi networking.
  Adafruit DRV2605L Haptic Motor Controller - STEMMA QT: The DRV2605 from TI is a fancy little motor driver. Rather than controlling a stepper motor or DC motor, its designed specifically for controlling haptic motors - buzzers and vibration motors. Normally one would just turn those kinds of motors on and off, but this driver has the ability to have various effects when driving a vibe motor. For example, ramping the vibration level up and down,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
  Vibration Motor: An eccentric vibration motor!
