# Fritzing sketch BME688 (saved by Fritzing 1.0.1rc)
breadboards: 1

parts:
  A1 = photon2
  Part2 = Adafruit BME680 [part_number="Adafruit #3660"]

nets:
  N1: A1.Pin_2, A1.Pin_31, Part2.VCC
  N2: A1.Pin_4, A1.Pin_30, A1.Pin_32, Part2.GND
  N3: A1.Pin_17, Part2.SDI/SDA
  N4: A1.Pin_18, Part2.SCK/SCL
  N5: A1.Pin_28, A1.Pin_29

notes:
  this particular wiring diagram might only be useful for wiring an BME688 via a 4-pin stemma/qt breakout cable. Note that the stemma/qt interfacing board is not shown here as it's a difficult thing to represent in fritzing (and also that there is no reason to use the stemma interfacing board if you are going to wire directly).
  this gives you an idea of how things are connected between the 4-pin connector at the photon board when you use the stemma/qt cable connection, but is not a representation of that.
  if you are connecting your photon2 to the BME688 with stemma you can ignore this diagram.

custom parts:
  photon2: The Photon 2 is a development module with a microcontroller and Wi-Fi networking.
