# Fritzing sketch microelectronics_intro (saved by Fritzing 1.0.1rc)
breadboards: 1

parts:
  A2 = photon2
  S2 = Pushbutton [package=THT]
  R2 = Resistor [tolerance=±5% power=0.25W resistance=330 package=THT]
  R3 = Resistor [tolerance=±5% power=0.25W resistance=220 package=THT]
  LED1 = LED - 5mm [color="Green (555nm)" current=0.030A package="5 mm [THT]"]

nets:
  N1: A2.Pin_2, A2.Pin_31, S2.leg1, R2.Pin_0
  N2: A2.Pin_4, A2.Pin_30, A2.Pin_32, R2.Pin_1, R3.Pin_1
  N3: A2.Pin_19, S2.leg0
  N4: A2.Pin_20, LED1.cathode
  N5: A2.Pin_28, A2.Pin_29
  N6: R3.Pin_0, LED1.anode

custom parts:
  photon2: The Photon 2 is a development module with a microcontroller and Wi-Fi networking.
